# Fritzing sketch grumkinPrototype (saved by Fritzing 0.9.1b)
breadboards: 1

parts:
  FET1 = STP16NF06 N-Channel Power MOSFET [part_number=1]
  R1 = Resistor [tolerance=±5% resistance=220 package=THT]
  ST_RGB0A = Screw terminal - 2 pins [package=THT]
  ST_RGB0B = Screw terminal - 2 pins [package=THT]
  ST0 = Screw terminal - 2 pins [package=THT]
  ST1 = Screw terminal - 2 pins [package=THT]
  ST2 = Screw terminal - 2 pins [package=THT]
  R2 = Resistor [tolerance=±5% resistance=220 package=THT]
  R3 = Resistor [tolerance=±5% resistance=220 package=THT]
  FET2 = STP16NF06 N-Channel Power MOSFET [part_number=2]
  FET3 = STP16NF06 N-Channel Power MOSFET [part_number=3]
  ST5 = Screw terminal - 2 pins [package=THT]
  ST4 = Screw terminal - 2 pins [package=THT]
  ST_RGB3B = Screw terminal - 2 pins [package=THT]
  ST3 = Screw terminal - 2 pins [package=THT]
  ST_RGB3A = Screw terminal - 2 pins [package=THT]
  R4 = Resistor [tolerance=±5% resistance=220 package=THT]
  R5 = Resistor [tolerance=±5% resistance=220 package=THT]
  R6 = Resistor [tolerance=±5% resistance=220 package=THT]
  FET4 = STP16NF06 N-Channel Power MOSFET [part_number=4]
  FET5 = STP16NF06 N-Channel Power MOSFET [part_number=5]
  FET6 = STP16NF06 N-Channel Power MOSFET [part_number=6]
  PWR_LED = Screw terminal - 2 pins [part_number=1 package=THT]
  J12 = female pin header, 2 pins [form="♀ (female)"]
  J13 = female pin header, 2 pins [form="♀ (female)"]
  J14 = female pin header, 2 pins [form="♀ (female)"]
  PWR_5v = female pin header, 2 pins [form="♀ (female)"]
  D1 = LED_BARGRAPH_10 [package=led_bargaph_10]

nets (from the schematic view):
  N1: FET1.gate, R1.Pin_0, D1.C_A
  N2: FET1.drain, ST_RGB0A.pin2, ST0.pin2
  N3: FET1.source, FET2.source, FET3.source, FET4.source, FET5.source, FET6.source, PWR_LED.pin1, PWR_5v.pin1, D1.H_C, D1.G_C, D1.F_C, D1.D_C
  N4: R1.Pin_1, J12.pin1
  N5: ST_RGB0A.pin1, ST0.pin1, ST1.pin1, ST2.pin1, ST5.pin1, ST4.pin1, ST3.pin1, ST_RGB3A.pin1, PWR_LED.pin2
  N6: ST_RGB0B.pin1, ST1.pin2, FET2.drain
  N7: ST_RGB0B.pin2, ST2.pin2, FET3.drain
  N8: R2.Pin_0, FET2.gate, D1.D_A
  N9: R2.Pin_1, J12.pin2
  N10: R3.Pin_0, D1.E_A
  N11: R3.Pin_1, J13.pin2
  N12: ST5.pin2, ST_RGB3B.pin2, FET6.drain
  N13: ST4.pin2, ST_RGB3B.pin1, FET5.drain
  N14: ST3.pin2, ST_RGB3A.pin2, FET4.drain
  N15: R4.Pin_0, FET4.gate, D1.F_A
  N16: R4.Pin_1, J13.pin1
  N17: R5.Pin_0, FET5.gate, D1.G_A
  N18: R5.Pin_1, J14.pin1
  N19: R6.Pin_0, FET6.gate, D1.H_A
  N20: R6.Pin_1, J14.pin2
  N21: D1.E_C, D1.C_C

custom parts:
  STP16NF06 N-Channel Power MOSFET: STP16NF06 N-channel Power MOSFET
